# Fritzing sketch pifritzing (saved by Fritzing 0.9.3b)

parts:
  Part1 = Adafruit PiTFT Plus 2.8inch [part_number="Adafruit #2298 and #2423"]
  Raspberry_Pi_1 = Raspberry Pi 3 [part_number=RPI-3-V1.2]

nets:
  3V3: Part1.3.3V, Raspberry_Pi_1.3v3, Raspberry_Pi_1.3V3
  +5V: Part1.+5V, Raspberry_Pi_1.5V
  N1: Part1.SDA, Raspberry_Pi_1.GPIO2
  N2: Part1.SCL, Raspberry_Pi_1.GPIO3
  GND: Part1.GND, Raspberry_Pi_1.GND
  N3: Part1.GPIO4, Raspberry_Pi_1.GPIO4
  N4: Part1.TXD, Raspberry_Pi_1.GPIO14
  N5: Part1.RXD, Raspberry_Pi_1.GPIO15
  N6: Part1.GPIO17, Raspberry_Pi_1.GPIO17
  N7: Part1.GPIO18, Raspberry_Pi_1.GPIO18
  N8: Part1.GPIO27, Raspberry_Pi_1.GPIO27
  N9: Part1.GPIO22, Raspberry_Pi_1.GPIO22
  N10: Part1.GPIO23, Raspberry_Pi_1.GPIO23
  N11: Part1.RT_INT, Raspberry_Pi_1.GPIO24
  N12: Part1.MOSI_, Raspberry_Pi_1.GPIO10
  N13: Part1.MISO, Raspberry_Pi_1.GPIO9
  N14: Part1.TFT_DC, Raspberry_Pi_1.GPIO25
  N15: Part1.SCLK, Raspberry_Pi_1.GPIO11
  N16: Part1.TFT_CS, Raspberry_Pi_1.GPIO8
  N17: Part1.RT_CS, Raspberry_Pi_1.GPIO7
  N18: Part1.EEDATA, Raspberry_Pi_1.ID_SD
  N19: Part1.EECLK, Raspberry_Pi_1.ID_SC
  N20: Part1.GPIO5, Raspberry_Pi_1.GPIO5
  N21: Part1.GPIO6, Raspberry_Pi_1.GPIO6
  N22: Part1.GPIO12, Raspberry_Pi_1.GPIO12
  N23: Part1.GPIO13, Raspberry_Pi_1.GPIO13
  N24: Part1.GPIO19, Raspberry_Pi_1.GPIO19
  N25: Part1.GPIO16, Raspberry_Pi_1.GPIO16
  N26: Part1.GPIO26, Raspberry_Pi_1.GPIO26
  N27: Part1.GPIO20, Raspberry_Pi_1.GPIO20
  N28: Part1.GPIO21, Raspberry_Pi_1.GPIO21

custom parts:
  Adafruit PiTFT Plus 2.8inch: Is this not the cutest little display for the Raspberry Pi? It features a 2.8" display with 320x240 16-bit color pixels and a resistive touch overlay. The plate uses the high speed SPI interface on the Pi and can use the mini display as a console, X window port, displaying images or video etc. Best of all it plugs right in on top! This updated design fits perfectly onto the Pi Zero, Pi 3, Pi 2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
