# Fritzing sketch pitftfritzing (saved by Fritzing 0.9.3b)
breadboards: 1

parts:
  Part1 = Adafruit 2.8 inch Captouch TFT [part_number="Adafruit #2090"]
  Raspberry_Pi_1 = Raspberry Pi 3 [part_number=RPI-3-V1.2]
  LED1 = LED - 5mm [color="Red (633nm)" package="5 mm [THT]"]
  R1 = Resistor [tolerance=±5% resistance=220 package=THT]
  LED2 = LED - 5mm [color="Red (633nm)" package="5 mm [THT]"]
  R2 = Resistor [tolerance=±5% resistance=220 package=THT]
  LED3 = LED - 5mm [color="Red (633nm)" package="5 mm [THT]"]
  R3 = Resistor [tolerance=±5% resistance=220 package=THT]
  LED4 = LED - 5mm [color="Red (633nm)" package="5 mm [THT]"]
  R4 = Resistor [tolerance=±5% resistance=220 package=THT]

nets:
  VIN: Part1.VIN, Raspberry_Pi_1.3v3
  N1: Part1.D0, Part1.D1, Part1.D2, Part1.D3, Raspberry_Pi_1.5V, R1.Pin_1, R2.Pin_1, R3.Pin_1, R4.Pin_1
  GND: Part1.GND, Raspberry_Pi_1.GND, LED1.anode, LED2.anode, LED3.anode, LED4.anode
  N2: Part1.3.3V, Part1.IM3, Part1.IM2, Part1.IM1
  N3: Part1.C/D_CLK, Raspberry_Pi_1.GIPO11
  N4: Part1.MOSI, Raspberry_Pi_1.GIPO10
  N5: Part1.CS, Raspberry_Pi_1.GIPO8
  N6: Part1.D/C_WR, Raspberry_Pi_1.GIPO18
  N7: Part1.RST, Raspberry_Pi_1.GIPO23
  N8: LED1.cathode, R1.Pin_0
  N9: LED2.cathode, R2.Pin_0
  N10: LED3.cathode, R3.Pin_0
  N11: LED4.cathode, R4.Pin_0

custom parts:
  Adafruit 2.8 inch Captouch TFT: Add some jazz & pizazz to your project with a color capactive touchscreen LCD. This TFT display is big (2.8" diagonal) bright (4 white-LED backlight) and colorful! 240x320 pixels with individual RGB pixel control, this has way more resolution than a black and white 128x64 display. As a bonus, this display has a capacitive single-touch touchscreen attached to it already, so you can detect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
